# Fritzing sketch CircuitDiagram (saved by Fritzing 0.9.2b)
breadboards: 1

parts:
  Part1 = Arduino Uno (Rev3)
  Q1 = PHOTOTRANSISTOR REFLECTIVE OBJECT SENSOR [package=qrb1114-side]
  Q2 = PHOTOTRANSISTOR REFLECTIVE OBJECT SENSOR [package=qrb1114-side]
  R1 = Resistor [tolerance=±5% resistance=200 package=THT]
  R2 = Resistor [tolerance=±5% resistance=20k package=THT]
  R3 = Resistor [tolerance=±5% resistance=200 package=THT]
  R5 = Resistor [tolerance=±5% resistance=20k package=THT]
  Part3 = Rotoshield - Motor driver shield for Arduino  # not connected

nets:
  N1: Part1.A0, Q1.A, R5.Pin_1
  N2: Part1.A1, Q2.A, R2.Pin_1
  N3: Part1.5V, R1.Pin_0, R2.Pin_0, R3.Pin_0, R5.Pin_0
  N4: Part1.GND, Q1.C, Q1.K, Q2.C, Q2.K
  N5: Q1.E, R3.Pin_1
  N6: Q2.E, R1.Pin_1

notes:
  20KΩ
  200Ω
